# Fritzing sketch XY_Platform_Circuit (saved by Fritzing 0.9.3b)
breadboards: 1

parts:
  M1 = Stepper Motor - Unipolar  # not connected
  M2 = Stepper Motor - Unipolar  # not connected
  Part1 = Arduino Uno (Rev3) - ICSP
  A1 = DM860A Stepper Motor Driver
  A2 = DM860A Stepper Motor Driver
  U1 = SWITCH-SPST-2 [package=switch-spst-vertical]
  J7 = Camdenboss CTB0158-4 [part_number=CTB0158-4 package=THT]
  J8 = Camdenboss CTB0158-4 [part_number=CTB0158-4 package=THT]
  J9 = Camdenboss CTB0158-4 [part_number=CTB0158-4 package=THT]
  J10 = Camdenboss CTB0158-4 [part_number=CTB0158-4 package=THT]
  A3 = Power Supply 2416
  JL012-13-5_1 = JL012-13-5.2 Lever (Limit) Switch SPDT + NO + NC [part_number=JL012-13-5.2]
  JL012-13-5_2 = JL012-13-5.2 Lever (Limit) Switch SPDT + NO + NC [part_number=JL012-13-5.2]
  J12 = 220v plug
  USBTTL1 = USB A Plug  # not connected
  J15 = Camdenboss CTB0158-3 [part_number=CTB0158-3 package=THT]
  J16 = female pin header, 2 pins [form="♀ (female)"]
  LED1 = LED - 3mm [color="Red (633nm)" package="3 mm [THT]"]
  LED2 = LED - 3mm [color="Red (633nm)" package="3 mm [THT]"]
  R1 = Resistor [tolerance=±5% resistance=220 package=THT]
  R2 = Resistor [tolerance=±5% resistance=220 package=THT]

nets:
  N1: Part1.A3, LED1.anode, R2.Pin_0
  N2: Part1.A4/SDA, LED2.anode, R1.Pin_0
  N3: Part1.D8, A1.DIR+(+5V)
  N4: Part1.D9_PWM, A1.PUL+(+5V)
  GND: Part1.GND, A2.GND, A2.DIR-(DIR), A2.PUL-(PUL), A3.Pin_1, LED1.cathode, LED2.cathode
  N5: Part1.D5_PWM, A2.PUL+(+5V)
  N6: Part1.D6_PWM, A2.DIR+(+5V)
  N7: Part1.5V, JL012-13-5_1.NO, JL012-13-5_2.NO
  N8: A1.B-, J8.terminal_1
  N9: A1.B+, J10.terminal_4
  N10: A1.A-, J8.terminal_4
  N11: A1.A+, J10.terminal_1
  N12: A1.GND, A1.DIR-(DIR), A1.PUL-(PUL)
  N13: A2.B-, J9.terminal_1
  N14: A2.B+, J7.terminal_4
  N15: A2.A-, J9.terminal_4
  N16: A2.A+, J7.terminal_1
  N17: A2.VDC, A3.Pin_2
  N18: U1.O, J15.terminal_3
  N19: U1.P, J16.pin1
  N20: J7.terminal_2, J9.terminal_3
  N21: J7.terminal_3, J9.terminal_2
  N22: J8.terminal_2, J10.terminal_3
  N23: J8.terminal_3, J10.terminal_2
  N24: JL012-13-5_1.C, R2.Pin_1
  N25: JL012-13-5_2.C, R1.Pin_1
  N26: J12.pin1, J15.terminal_2, J16.pin2
  N27: J12.pin2, J15.terminal_1

custom parts:
  DM860A Stepper Motor Driver: DM860A is a type of two-phase hybrid stepping motor driver, The drive voltage of which is from 24VDC to 80VDC. It is designed for use with 2-phase hybrid stepper motor of all kinds with 57mm to 110mm outside diameter and less than 8.0A phase current. Mar 2023: Correct pcb layerId as the part won't save correctly in a .fzz file as is.
  Power Supply 2416: AC 110V-220V To DC 36V Switching Power Supply Board AC-DC Power Module 36V 5A 180W AC-DC2416.
  JL012-13-5.2 Lever (Limit) Switch SPDT + NO + NC: Micro Switch; Model No.: JL012-13.5-2; Actuator Action: Momentary; Actuator Type: Hinge Lever; Contact Configuration: 1NO, 1NC (SPDT) Temperature -25~65℃；Relative humidity: below 85%; Rate Voltage: 125V AC; Rated Current: 1A.
  220v plug: Generic 220V AC plug.
